// Logisim project addressing_memory1.circ as structural Verilog: 1 circuit, main circuit main
module main (
  input  Data_in,
  input  Address,
  input  Write,
  output out_4,
  output out_5
);

  wire and_1_out, and_2_out, and_3_out, and_4_out, and_5_out, and_6_out, nor_2_out, nor_3_out, not_1_out,
       not_2_out, not_3_out;

  not not_1 (not_1_out, Address);
  not not_2 (not_2_out, Data_in);
  and and_1 (and_1_out, not_1_out, Write);
  and and_2 (and_2_out, not_2_out, and_1_out);
  and and_3 (and_3_out, and_1_out, Data_in);
  nor nor_1 (out_4, and_2_out, nor_2_out);
  nor nor_2 (nor_2_out, out_4, and_3_out);
  and and_4 (and_4_out, Address, Write);
  not not_3 (not_3_out, Data_in);
  and and_5 (and_5_out, not_3_out, and_4_out);
  and and_6 (and_6_out, and_4_out, Data_in);
  nor nor_3 (nor_3_out, out_5, and_6_out);
  nor nor_4 (out_5, and_5_out, nor_3_out);

  // Notes on the sheet:
  //   Set
  //   Data
  //   Flip-flop 0
  //   Set
  //   Data
  //   Flip-flop 1
endmodule
