// Logisim project addressing_memory2.circ as structural Verilog: 1 circuit, main circuit main
module main (
  input  Data_in,
  input  Address,
  input  Write,
  output out_4,
  output out_5
);

  wire and_1_out, and_2_out, nand_1_out, nand_2_out, nand_4_out, nand_5_out, nand_6_out, nand_8_out,
       not_1_out;

  and and_1 (and_1_out, not_1_out, Write);
  not not_1 (not_1_out, Address);
  nand nand_1 (nand_1_out, Data_in, and_1_out);
  nand nand_2 (nand_2_out, nand_1_out, and_1_out);
  nand nand_3 (out_4, nand_1_out, nand_4_out);
  nand nand_4 (nand_4_out, out_4, nand_2_out);
  and and_2 (and_2_out, Address, Write);
  nand nand_5 (nand_5_out, Data_in, and_2_out);
  nand nand_6 (nand_6_out, nand_5_out, and_2_out);
  nand nand_7 (out_5, nand_5_out, nand_8_out);
  nand nand_8 (nand_8_out, out_5, nand_6_out);

  // Notes on the sheet:
  //   Data
  //   Set
  //   Flip-flop 0
  //   Set
  //   Data
  //   Flip-flop 1
endmodule
