// Logisim project byte2.circ as structural Verilog: 1 circuit, main circuit main
module main (
  input  in_1,
  input  in_2,
  input  in_3,
  input  in_4,
  input  in_5,
  input  in_6,
  input  in_7,
  input  in_8,
  input  in_9,
  output out_10,
  output out_11,
  output out_12,
  output out_13,
  output out_14,
  output out_15,
  output out_16,
  output out_17
);

  wire and_1_out, and_2_out, and_3_out, and_4_out, and_5_out, and_6_out, and_7_out, and_8_out, and_9_out,
       and_10_out, and_11_out, and_12_out, and_13_out, and_14_out, and_15_out, and_16_out, nor_2_out,
       nor_4_out, nor_6_out, nor_8_out, nor_10_out, nor_12_out, nor_14_out, nor_16_out, not_1_out, not_2_out,
       not_3_out, not_4_out, not_5_out, not_6_out, not_7_out, not_8_out;

  not not_1 (not_1_out, in_1);
  not not_2 (not_2_out, in_2);
  not not_3 (not_3_out, in_3);
  not not_4 (not_4_out, in_4);
  not not_5 (not_5_out, in_5);
  not not_6 (not_6_out, in_6);
  not not_7 (not_7_out, in_7);
  not not_8 (not_8_out, in_8);
  and and_1 (and_1_out, not_1_out, in_9);
  and and_2 (and_2_out, in_9, in_1);
  and and_3 (and_3_out, not_2_out, in_9);
  and and_4 (and_4_out, in_9, in_2);
  and and_5 (and_5_out, not_3_out, in_9);
  and and_6 (and_6_out, in_9, in_3);
  and and_7 (and_7_out, not_4_out, in_9);
  and and_8 (and_8_out, in_9, in_4);
  and and_9 (and_9_out, not_5_out, in_9);
  and and_10 (and_10_out, in_9, in_5);
  and and_11 (and_11_out, not_6_out, in_9);
  and and_12 (and_12_out, in_9, in_6);
  and and_13 (and_13_out, not_7_out, in_9);
  and and_14 (and_14_out, in_9, in_7);
  and and_15 (and_15_out, not_8_out, in_9);
  and and_16 (and_16_out, in_9, in_8);
  nor nor_1 (out_10, and_1_out, nor_2_out);
  nor nor_2 (nor_2_out, out_10, and_2_out);
  nor nor_3 (out_11, and_3_out, nor_4_out);
  nor nor_4 (nor_4_out, out_11, and_4_out);
  nor nor_5 (out_12, and_5_out, nor_6_out);
  nor nor_6 (nor_6_out, out_12, and_6_out);
  nor nor_7 (out_13, and_7_out, nor_8_out);
  nor nor_8 (nor_8_out, out_13, and_8_out);
  nor nor_9 (out_14, and_9_out, nor_10_out);
  nor nor_10 (nor_10_out, out_14, and_10_out);
  nor nor_11 (out_15, and_11_out, nor_12_out);
  nor nor_12 (nor_12_out, out_15, and_12_out);
  nor nor_13 (out_16, and_13_out, nor_14_out);
  nor nor_14 (nor_14_out, out_16, and_14_out);
  nor nor_15 (out_17, and_15_out, nor_16_out);
  nor nor_16 (nor_16_out, out_17, and_16_out);

  // Notes on the sheet:
  //   8 bit data input
  //   Set wire to save data
  //   Set
  //   Data
  //   Set
  //   Data
  //   Set
  //   Data
  //   Set
  //   Data
  //   Set
  //   Data
  //   Set
  //   Data
  //   Set
  //   Data
  //   Set
  //   Data
  //   8 bit memory
endmodule
