// Logisim project flip-flop-type2.circ as structural Verilog: 1 circuit, main circuit main
module main (
);

  wire and_1_out, and_2_out, nor_1_out, nor_2_out, not_1_out, undriven, undriven_2;

  not not_1 (not_1_out, undriven);
  and and_1 (and_1_out, not_1_out, undriven_2);
  and and_2 (and_2_out, undriven_2, undriven);
  nor nor_1 (nor_1_out, and_1_out, nor_2_out);
  nor nor_2 (nor_2_out, nor_1_out, and_2_out);

  // Notes on the sheet:
  //   Set
  //   Data
  //   Level-tiggerred D-type flip-flop
endmodule
