// Logisim project flip-flop-type3.circ as structural Verilog: 1 circuit, main circuit main
module main (
  input  Data,
  input  Set
);

  wire and_1_out, and_2_out, and_3_out, not_1_out, not_2_out, or_1_out;

  not not_1 (not_1_out, Data);
  and and_1 (and_1_out, Data, Set);
  and and_2 (and_2_out, not_1_out, Set);
  or or_1 (or_1_out, and_3_out, and_1_out);
  not not_2 (not_2_out, and_2_out);
  and and_3 (and_3_out, or_1_out, not_2_out);

  // Notes on the sheet:
  //   Gated Latch
endmodule
