// Logisim project flip-flop1.circ as structural Verilog: 1 circuit, main circuit main
module main (
  input  Data,
  input  Set,
  output Q,
  output Q_bar
);

  wire _1_out, _2_out;

  nand _1 (_1_out, Data, Set);
  nand _2 (_2_out, _1_out, Set);
  nand _3 (Q, _1_out, Q_bar);
  nand _4 (Q_bar, Q, _2_out);

  // Notes on the sheet:
  //   A simple flip-flop
endmodule
