// Logisim project flip-flop2.circ as structural Verilog: 1 circuit, main circuit main
module main (
  input  R,
  input  S,
  output Q,
  output Q_bar
);

  nor nor_1 (Q, R, Q_bar);
  nor nor_2 (Q_bar, Q, S);

  // Notes on the sheet:
  //   Another feedback flip-flop
endmodule
