// Logisim project flip-flop3.circ as structural Verilog: 1 circuit, main circuit main
module main (
  input  Set,
  input  Data,
  output Q,
  output Q_bar
);

  wire and_1_out, and_2_out, not_1_out;

  not not_1 (not_1_out, Data);
  and and_1 (and_1_out, not_1_out, Set);
  and and_2 (and_2_out, Set, Data);
  nor nor_1 (Q, and_1_out, Q_bar);
  nor nor_2 (Q_bar, Q, and_2_out);

  // Notes on the sheet:
  //   Level-tiggerred D-type flip-flop
endmodule
