// Logisim project mov_registers.circ as structural Verilog: 1 circuit, main circuit main
module main (
  input  in_1,
  input  in_2,
  input  in_3,
  input  in_4,
  input  in_5,
  input  in_6,
  input  in_7,
  input  in_8,
  input  Hit_ENTER,
  input  in_10,
  input  in_11,
  input  in_12,
  input  in_13,
  input  in_14,
  input  in_15,
  input  in_16,
  input  in_17,
  input  in_18,
  output out_19,
  output out_20,
  output out_21,
  output out_22,
  output out_23,
  output out_24,
  output out_25,
  output out_26
);

  wire _1_2_out, _1_3_out, _1_4_out, _1_5_out, _1_6_out, _1_7_out, _1_8_out, _1_9_out, _1_10_out, _1_11_out,
       _1_12_out, _1_13_out, _1_14_out, _1_15_out, _1_16_out, _1_out, _2_2_out, _2_3_out, _2_4_out, _2_5_out,
       _2_6_out, _2_7_out, _2_8_out, _2_9_out, _2_10_out, _2_11_out, _2_12_out, _2_13_out, _2_14_out,
       _2_15_out, _2_16_out, _2_out, _3_2_out, _3_3_out, _3_4_out, _3_5_out, _3_6_out, _3_7_out, _3_8_out,
       _3_9_out, _3_10_out, _3_11_out, _3_12_out, _3_13_out, _3_14_out, _3_15_out, _3_16_out, _3_out,
       _4_2_out, _4_3_out, _4_4_out, _4_5_out, _4_6_out, _4_7_out, _4_8_out, _4_9_out, _4_10_out, _4_11_out,
       _4_12_out, _4_13_out, _4_14_out, _4_15_out, _4_16_out, _4_out, and_1_out, and_2_out, and_3_out,
       and_4_out, and_5_out, and_6_out, and_7_out, and_8_out, and_25_out, and_26_out, and_27_out, and_28_out,
       and_29_out, and_30_out, and_31_out, and_32_out, and_33_out, and_34_out, and_35_out, and_36_out,
       and_37_out, and_38_out, and_39_out, and_40_out, and_49_out, and_50_out, and_51_out, and_52_out,
       and_53_out, and_54_out, and_55_out, and_56_out, and_57_out, and_58_out, and_59_out, and_60_out,
       and_61_out, and_62_out, and_63_out, and_64_out, nor_1_out, nor_2_out, nor_3_out, nor_4_out, nor_5_out,
       nor_6_out, nor_7_out, nor_8_out, nor_9_out, nor_10_out, nor_11_out, nor_12_out, nor_13_out,
       nor_14_out, nor_15_out, nor_16_out, nor_17_out, nor_18_out, nor_19_out, nor_20_out, nor_21_out,
       nor_22_out, nor_23_out, nor_24_out, nor_25_out, nor_26_out, nor_27_out, nor_28_out, nor_29_out,
       nor_30_out, nor_31_out, nor_32_out, not_1_out, not_2_out, not_3_out, not_4_out, not_5_out, not_6_out,
       not_7_out, not_8_out, not_9_out, not_10_out, not_11_out, not_12_out, not_13_out, not_14_out,
       not_15_out, not_16_out;

  and and_1 (and_1_out, in_1, Hit_ENTER);
  and and_2 (and_2_out, in_2, Hit_ENTER);
  and and_3 (and_3_out, in_3, Hit_ENTER);
  and and_4 (and_4_out, in_4, Hit_ENTER);
  and and_5 (and_5_out, in_5, Hit_ENTER);
  and and_6 (and_6_out, in_6, Hit_ENTER);
  and and_7 (and_7_out, in_7, Hit_ENTER);
  and and_8 (and_8_out, in_8, Hit_ENTER);
  nand _1 (_1_out, and_8_out, in_11);
  nand _1_2 (_1_2_out, and_7_out, in_11);
  nand _1_3 (_1_3_out, and_6_out, in_11);
  nand _1_4 (_1_4_out, and_5_out, in_11);
  nand _1_5 (_1_5_out, and_4_out, in_11);
  nand _1_6 (_1_6_out, and_3_out, in_11);
  nand _1_7 (_1_7_out, and_2_out, in_11);
  nand _1_8 (_1_8_out, and_1_out, in_11);
  nand _2 (_2_out, _1_out, in_11);
  nand _2_2 (_2_2_out, _1_2_out, in_11);
  nand _2_3 (_2_3_out, _1_3_out, in_11);
  nand _2_4 (_2_4_out, _1_4_out, in_11);
  nand _2_5 (_2_5_out, _1_5_out, in_11);
  nand _2_6 (_2_6_out, _1_6_out, in_11);
  nand _2_7 (_2_7_out, _1_7_out, in_11);
  nand _2_8 (_2_8_out, _1_8_out, in_11);
  nand _3 (_3_out, _1_out, _4_out);
  nand _4 (_4_out, _3_out, _2_out);
  nand _3_2 (_3_2_out, _1_2_out, _4_2_out);
  nand _4_2 (_4_2_out, _3_2_out, _2_2_out);
  nand _3_3 (_3_3_out, _1_3_out, _4_3_out);
  nand _4_3 (_4_3_out, _3_3_out, _2_3_out);
  nand _3_4 (_3_4_out, _1_4_out, _4_4_out);
  nand _4_4 (_4_4_out, _3_4_out, _2_4_out);
  nand _3_5 (_3_5_out, _1_5_out, _4_5_out);
  nand _4_5 (_4_5_out, _3_5_out, _2_5_out);
  nand _3_6 (_3_6_out, _1_6_out, _4_6_out);
  nand _4_6 (_4_6_out, _3_6_out, _2_6_out);
  nand _3_7 (_3_7_out, _1_7_out, _4_7_out);
  nand _4_7 (_4_7_out, _3_7_out, _2_7_out);
  nand _3_8 (_3_8_out, _1_8_out, _4_8_out);
  nand _4_8 (_4_8_out, _3_8_out, _2_8_out);
  and and_9 (and_8_out, _3_out, in_13);
  and and_10 (and_7_out, _3_2_out, in_13);
  and and_11 (and_6_out, _3_3_out, in_13);
  and and_12 (and_5_out, _3_4_out, in_13);
  and and_13 (and_4_out, _3_5_out, in_13);
  and and_14 (and_3_out, _3_6_out, in_13);
  and and_15 (and_2_out, _3_7_out, in_13);
  and and_16 (and_1_out, _3_8_out, in_13);
  nand _1_9 (_1_9_out, and_8_out, in_12);
  nand _1_10 (_1_10_out, and_7_out, in_12);
  nand _1_11 (_1_11_out, and_6_out, in_12);
  nand _1_12 (_1_12_out, and_5_out, in_12);
  nand _1_13 (_1_13_out, and_4_out, in_12);
  nand _1_14 (_1_14_out, and_3_out, in_12);
  nand _1_15 (_1_15_out, and_2_out, in_12);
  nand _1_16 (_1_16_out, and_1_out, in_12);
  nand _2_9 (_2_9_out, _1_9_out, in_12);
  nand _2_10 (_2_10_out, _1_10_out, in_12);
  nand _2_11 (_2_11_out, _1_11_out, in_12);
  nand _2_12 (_2_12_out, _1_12_out, in_12);
  nand _2_13 (_2_13_out, _1_13_out, in_12);
  nand _2_14 (_2_14_out, _1_14_out, in_12);
  nand _2_15 (_2_15_out, _1_15_out, in_12);
  nand _2_16 (_2_16_out, _1_16_out, in_12);
  nand _3_9 (_3_9_out, _1_9_out, _4_9_out);
  nand _4_9 (_4_9_out, _3_9_out, _2_9_out);
  nand _3_10 (_3_10_out, _1_10_out, _4_10_out);
  nand _4_10 (_4_10_out, _3_10_out, _2_10_out);
  nand _3_11 (_3_11_out, _1_11_out, _4_11_out);
  nand _4_11 (_4_11_out, _3_11_out, _2_11_out);
  nand _3_12 (_3_12_out, _1_12_out, _4_12_out);
  nand _4_12 (_4_12_out, _3_12_out, _2_12_out);
  nand _3_13 (_3_13_out, _1_13_out, _4_13_out);
  nand _4_13 (_4_13_out, _3_13_out, _2_13_out);
  nand _3_14 (_3_14_out, _1_14_out, _4_14_out);
  nand _4_14 (_4_14_out, _3_14_out, _2_14_out);
  nand _3_15 (_3_15_out, _1_15_out, _4_15_out);
  nand _4_15 (_4_15_out, _3_15_out, _2_15_out);
  nand _3_16 (_3_16_out, _1_16_out, _4_16_out);
  nand _4_16 (_4_16_out, _3_16_out, _2_16_out);
  and and_17 (and_8_out, _3_9_out, in_14);
  and and_18 (and_7_out, _3_10_out, in_14);
  and and_19 (and_6_out, _3_11_out, in_14);
  and and_20 (and_5_out, _3_12_out, in_14);
  and and_21 (and_4_out, _3_13_out, in_14);
  and and_22 (and_3_out, _3_14_out, in_14);
  and and_23 (and_2_out, _3_15_out, in_14);
  and and_24 (and_1_out, _3_16_out, in_14);
  not not_1 (not_1_out, and_8_out);
  not not_2 (not_2_out, and_7_out);
  not not_3 (not_3_out, and_6_out);
  not not_4 (not_4_out, and_5_out);
  not not_5 (not_5_out, and_4_out);
  not not_6 (not_6_out, and_3_out);
  not not_7 (not_7_out, and_2_out);
  not not_8 (not_8_out, and_1_out);
  and and_25 (and_25_out, not_1_out, in_16);
  and and_26 (and_26_out, in_16, and_8_out);
  and and_27 (and_27_out, not_2_out, in_16);
  and and_28 (and_28_out, in_16, and_7_out);
  and and_29 (and_29_out, not_3_out, in_16);
  and and_30 (and_30_out, in_16, and_6_out);
  and and_31 (and_31_out, not_4_out, in_16);
  and and_32 (and_32_out, in_16, and_5_out);
  and and_33 (and_33_out, not_5_out, in_16);
  and and_34 (and_34_out, in_16, and_4_out);
  and and_35 (and_35_out, not_6_out, in_16);
  and and_36 (and_36_out, in_16, and_3_out);
  and and_37 (and_37_out, not_7_out, in_16);
  and and_38 (and_38_out, in_16, and_2_out);
  and and_39 (and_39_out, not_8_out, in_16);
  and and_40 (and_40_out, in_16, and_1_out);
  nor nor_1 (nor_1_out, and_25_out, nor_2_out);
  nor nor_2 (nor_2_out, nor_1_out, and_26_out);
  nor nor_3 (nor_3_out, and_27_out, nor_4_out);
  nor nor_4 (nor_4_out, nor_3_out, and_28_out);
  nor nor_5 (nor_5_out, and_29_out, nor_6_out);
  nor nor_6 (nor_6_out, nor_5_out, and_30_out);
  nor nor_7 (nor_7_out, and_31_out, nor_8_out);
  nor nor_8 (nor_8_out, nor_7_out, and_32_out);
  nor nor_9 (nor_9_out, and_33_out, nor_10_out);
  nor nor_10 (nor_10_out, nor_9_out, and_34_out);
  nor nor_11 (nor_11_out, and_35_out, nor_12_out);
  nor nor_12 (nor_12_out, nor_11_out, and_36_out);
  nor nor_13 (nor_13_out, and_37_out, nor_14_out);
  nor nor_14 (nor_14_out, nor_13_out, and_38_out);
  nor nor_15 (nor_15_out, and_39_out, nor_16_out);
  nor nor_16 (nor_16_out, nor_15_out, and_40_out);
  and and_41 (and_8_out, nor_1_out, in_18);
  and and_42 (and_7_out, nor_3_out, in_18);
  and and_43 (and_6_out, nor_5_out, in_18);
  and and_44 (and_5_out, nor_7_out, in_18);
  and and_45 (and_4_out, nor_9_out, in_18);
  and and_46 (and_3_out, nor_11_out, in_18);
  and and_47 (and_2_out, nor_13_out, in_18);
  and and_48 (and_1_out, nor_15_out, in_18);
  not not_9 (not_9_out, and_8_out);
  not not_10 (not_10_out, and_7_out);
  not not_11 (not_11_out, and_6_out);
  not not_12 (not_12_out, and_5_out);
  not not_13 (not_13_out, and_4_out);
  not not_14 (not_14_out, and_3_out);
  not not_15 (not_15_out, and_2_out);
  not not_16 (not_16_out, and_1_out);
  and and_49 (and_49_out, not_9_out, in_15);
  and and_50 (and_50_out, in_15, and_8_out);
  and and_51 (and_51_out, not_10_out, in_15);
  and and_52 (and_52_out, in_15, and_7_out);
  and and_53 (and_53_out, not_11_out, in_15);
  and and_54 (and_54_out, in_15, and_6_out);
  and and_55 (and_55_out, not_12_out, in_15);
  and and_56 (and_56_out, in_15, and_5_out);
  and and_57 (and_57_out, not_13_out, in_15);
  and and_58 (and_58_out, in_15, and_4_out);
  and and_59 (and_59_out, not_14_out, in_15);
  and and_60 (and_60_out, in_15, and_3_out);
  and and_61 (and_61_out, not_15_out, in_15);
  and and_62 (and_62_out, in_15, and_2_out);
  and and_63 (and_63_out, not_16_out, in_15);
  and and_64 (and_64_out, in_15, and_1_out);
  nor nor_17 (nor_17_out, and_49_out, nor_18_out);
  nor nor_18 (nor_18_out, nor_17_out, and_50_out);
  nor nor_19 (nor_19_out, and_51_out, nor_20_out);
  nor nor_20 (nor_20_out, nor_19_out, and_52_out);
  nor nor_21 (nor_21_out, and_53_out, nor_22_out);
  nor nor_22 (nor_22_out, nor_21_out, and_54_out);
  nor nor_23 (nor_23_out, and_55_out, nor_24_out);
  nor nor_24 (nor_24_out, nor_23_out, and_56_out);
  nor nor_25 (nor_25_out, and_57_out, nor_26_out);
  nor nor_26 (nor_26_out, nor_25_out, and_58_out);
  nor nor_27 (nor_27_out, and_59_out, nor_28_out);
  nor nor_28 (nor_28_out, nor_27_out, and_60_out);
  nor nor_29 (nor_29_out, and_61_out, nor_30_out);
  nor nor_30 (nor_30_out, nor_29_out, and_62_out);
  nor nor_31 (nor_31_out, and_63_out, nor_32_out);
  nor nor_32 (nor_32_out, nor_31_out, and_64_out);
  and and_65 (and_8_out, nor_17_out, in_17);
  and and_66 (and_7_out, nor_19_out, in_17);
  and and_67 (and_6_out, nor_21_out, in_17);
  and and_68 (and_5_out, nor_23_out, in_17);
  and and_69 (and_4_out, nor_25_out, in_17);
  and and_70 (and_3_out, nor_27_out, in_17);
  and and_71 (and_2_out, nor_29_out, in_17);
  and and_72 (and_1_out, nor_31_out, in_17);
  and and_73 (out_20, in_10, and_2_out);
  and and_74 (out_19, in_10, and_1_out);
  and and_75 (out_21, in_10, and_3_out);
  and and_76 (out_22, in_10, and_4_out);
  and and_77 (out_23, in_10, and_5_out);
  and and_78 (out_24, in_10, and_6_out);
  and and_79 (out_25, in_10, and_7_out);
  and and_80 (out_26, in_10, and_8_out);

  // Notes on the sheet:
  //   stdin.getu8();
  //   8 bit data input
  //   Set wire to save data
  //   Enable wire to get data
  //   Data
  //   Data
  //   Data
  //   Data
  //   Data
  //   Data
  //   Data
  //   Data
  //   Set
  //   Set
  //   Set
  //   Set
  //   Set
  //   Set
  //   Set
  //   Set
  //   8 bit register
  //   AH
  //   8 bit data output
  //   8 bit data input
  //   Set wire to save data
  //   Enable wire to get data
  //   Data
  //   Set
  //   Data
  //   Set
  //   Data
  //   Set
  //   Data
  //   Set
  //   Data
  //   Set
  //   Data
  //   Set
  //   Data
  //   Set
  //   Data
  //   Set
  //   8 bit register
  //   AL
  //   8 bit data output
  //   8 bit data input
  //   Set wire to save data
  //   Enable wire to get data
  //   Set
  //   Data
  //   Set
  //   Data
  //   Set
  //   Data
  //   Set
  //   Data
  //   Set
  //   Data
  //   Set
  //   Data
  //   Set
  //   Data
  //   Set
  //   Data
  //   8 bit register
  //   BH
  //   8 bit data output
  //   8 bit data input
  //   Set wire to save data
  //   Enable wire to get data
  //   Set
  //   Data
  //   Set
  //   Data
  //   Set
  //   Data
  //   Set
  //   Data
  //   Set
  //   Data
  //   Set
  //   Data
  //   Set
  //   Data
  //   Set
  //   Data
  //   8 bit register
  //   8 bit data output
  //   BL
  //   stdout.put();
endmodule
