// Logisim project register1.circ as structural Verilog: 1 circuit, main circuit main
module main (
  input  in_1,
  input  in_2,
  input  in_3,
  input  in_4,
  input  in_5,
  input  in_6,
  input  in_7,
  input  in_8,
  input  in_9,
  input  in_10,
  output out_11,
  output out_12,
  output out_13,
  output out_14,
  output out_15,
  output out_16,
  output out_17,
  output out_18
);

  wire _1_2_out, _1_3_out, _1_4_out, _1_5_out, _1_6_out, _1_7_out, _1_8_out, _1_out, _2_2_out, _2_3_out,
       _2_4_out, _2_5_out, _2_6_out, _2_7_out, _2_8_out, _2_out, _3_2_out, _3_3_out, _3_4_out, _3_5_out,
       _3_6_out, _3_7_out, _3_8_out, _3_out, _4_2_out, _4_3_out, _4_4_out, _4_5_out, _4_6_out, _4_7_out,
       _4_8_out, _4_out;

  nand _1 (_1_out, in_1, in_9);
  nand _1_2 (_1_2_out, in_2, in_9);
  nand _1_3 (_1_3_out, in_3, in_9);
  nand _1_4 (_1_4_out, in_4, in_9);
  nand _1_5 (_1_5_out, in_5, in_9);
  nand _1_6 (_1_6_out, in_6, in_9);
  nand _1_7 (_1_7_out, in_7, in_9);
  nand _1_8 (_1_8_out, in_8, in_9);
  nand _2 (_2_out, _1_out, in_9);
  nand _2_2 (_2_2_out, _1_2_out, in_9);
  nand _2_3 (_2_3_out, _1_3_out, in_9);
  nand _2_4 (_2_4_out, _1_4_out, in_9);
  nand _2_5 (_2_5_out, _1_5_out, in_9);
  nand _2_6 (_2_6_out, _1_6_out, in_9);
  nand _2_7 (_2_7_out, _1_7_out, in_9);
  nand _2_8 (_2_8_out, _1_8_out, in_9);
  nand _3 (_3_out, _1_out, _4_out);
  nand _4 (_4_out, _3_out, _2_out);
  nand _3_2 (_3_2_out, _1_2_out, _4_2_out);
  nand _4_2 (_4_2_out, _3_2_out, _2_2_out);
  nand _3_3 (_3_3_out, _1_3_out, _4_3_out);
  nand _4_3 (_4_3_out, _3_3_out, _2_3_out);
  nand _3_4 (_3_4_out, _1_4_out, _4_4_out);
  nand _4_4 (_4_4_out, _3_4_out, _2_4_out);
  nand _3_5 (_3_5_out, _1_5_out, _4_5_out);
  nand _4_5 (_4_5_out, _3_5_out, _2_5_out);
  nand _3_6 (_3_6_out, _1_6_out, _4_6_out);
  nand _4_6 (_4_6_out, _3_6_out, _2_6_out);
  nand _3_7 (_3_7_out, _1_7_out, _4_7_out);
  nand _4_7 (_4_7_out, _3_7_out, _2_7_out);
  nand _3_8 (_3_8_out, _1_8_out, _4_8_out);
  nand _4_8 (_4_8_out, _3_8_out, _2_8_out);
  and and_1 (out_11, _3_out, in_10);
  and and_2 (out_12, _3_2_out, in_10);
  and and_3 (out_13, _3_3_out, in_10);
  and and_4 (out_14, _3_4_out, in_10);
  and and_5 (out_15, _3_5_out, in_10);
  and and_6 (out_16, _3_6_out, in_10);
  and and_7 (out_17, _3_7_out, in_10);
  and and_8 (out_18, _3_8_out, in_10);

  // Notes on the sheet:
  //   8 bit data input
  //   Set wire to save data
  //   Enable wire to get data
  //   Data
  //   Set
  //   Data
  //   Set
  //   Data
  //   Set
  //   Data
  //   Set
  //   Data
  //   Set
  //   Data
  //   Set
  //   Data
  //   Set
  //   Data
  //   Set
  //   8 bit register
  //   8 bit data output
endmodule
